// Logisim project cpu.circ as structural Verilog
module main (
  input  [15:0] inM,
  input  [15:0] instruction,
  input  reset,
  output [15:0] outM,
  output writeM,
  output [14:0] addressM,
  output [14:0] pc
);
endmodule

module ram64 (
  input  [15:0] Input,
  input  Load,
  input  [5:0] Address,
  output [15:0] Output
);

  wire clock_1_out, demultiplexer_1_out0, demultiplexer_1_out1, demultiplexer_1_out2, demultiplexer_1_out3,
       demultiplexer_1_out4, demultiplexer_1_out5, demultiplexer_1_out6, demultiplexer_1_out7;
  wire [15:0] ram_1_data, ram_2_data, ram_3_data, ram_4_data, ram_5_data, ram_6_data, ram_7_data, ram_8_data;

  Demultiplexer #(.select(3)) demultiplexer_1 (
    .out0(demultiplexer_1_out0), .out1(demultiplexer_1_out1), .out2(demultiplexer_1_out2),
    .out3(demultiplexer_1_out3), .out4(demultiplexer_1_out4), .out5(demultiplexer_1_out5),
    .out6(demultiplexer_1_out6), .out7(demultiplexer_1_out7), .in(Load), .sel(Address[5:3]));  // open: en
  RAM #(.addrWidth(3), .dataWidth(16), .bus("separate")) ram_1 (
    .addr(Address[2:0]), .din(Input), .data(ram_1_data), .str(demultiplexer_1_out0), .clk(clock_1_out));  // open: sel, ld, clr
  RAM #(.addrWidth(3), .dataWidth(16), .bus("separate")) ram_2 (
    .addr(Address[2:0]), .din(Input), .data(ram_2_data), .str(demultiplexer_1_out2), .clk(clock_1_out));  // open: sel, ld, clr
  RAM #(.addrWidth(3), .dataWidth(16), .bus("separate")) ram_3 (
    .addr(Address[2:0]), .din(Input), .data(ram_3_data), .str(demultiplexer_1_out4), .clk(clock_1_out));  // open: sel, ld, clr
  RAM #(.addrWidth(3), .dataWidth(16), .bus("separate")) ram_4 (
    .addr(Address[2:0]), .din(Input), .data(ram_4_data), .str(demultiplexer_1_out6), .clk(clock_1_out));  // open: sel, ld, clr
  Clock clock_1 (.out(clock_1_out));
  RAM #(.addrWidth(3), .dataWidth(16), .bus("separate")) ram_5 (
    .addr(Address[2:0]), .din(Input), .data(ram_5_data), .str(demultiplexer_1_out1), .clk(clock_1_out));  // open: sel, ld, clr
  RAM #(.addrWidth(3), .dataWidth(16), .bus("separate")) ram_6 (
    .addr(Address[2:0]), .din(Input), .data(ram_6_data), .str(demultiplexer_1_out3), .clk(clock_1_out));  // open: sel, ld, clr
  RAM #(.addrWidth(3), .dataWidth(16), .bus("separate")) ram_7 (
    .addr(Address[2:0]), .din(Input), .data(ram_7_data), .str(demultiplexer_1_out5), .clk(clock_1_out));  // open: sel, ld, clr
  RAM #(.addrWidth(3), .dataWidth(16), .bus("separate")) ram_8 (
    .addr(Address[2:0]), .din(Input), .data(ram_8_data), .str(demultiplexer_1_out7), .clk(clock_1_out));  // open: sel, ld, clr
  Multiplexer #(.select(3), .width(16)) multiplexer_1 (
    .in0(ram_1_data), .in1(ram_5_data), .in2(ram_2_data), .in3(ram_6_data), .in4(ram_3_data),
    .in5(ram_7_data), .in6(ram_4_data), .in7(ram_8_data), .out(Output), .sel(Address[5:3]));  // open: en

  // Notes on the sheet:
  //   RAM64
endmodule
