// Logisim project hack-pc.circ as structural Verilog
module cpu (
  input  [15:0] in_1,
  input  reset,
  output [14:0] out_3
);

  wire ALUtoA, CLK, JEQ, JGT, JLE, JLT, JumpToA, loadA, loadD, ng, not_1_out, not_2_out, not_3_out, or_1_out,
       PCload, writeM, zr;
  wire [15:0] A_output, alu_1_out, D_output, mux16_1_o, mux16_2_o, ram_1_out;
  wire [15:15] pc_1_output;

  and and_1 (JLT, ng, in_1[2]);
  and and_2 (writeM, in_1[15], in_1[3]);
  and and_3 (loadD, in_1[4], in_1[15]);
  or or_1 (or_1_out, zr, ng);
  not not_1 (not_1_out, in_1[15]);
  mux16 mux16_1 (.o(mux16_1_o), .sel(ALUtoA), .b(alu_1_out), .a(in_1));
  and and_4 (JGT, in_1[0], not_2_out);
  not not_2 (not_2_out, or_1_out);
  and and_5 (JEQ, zr, in_1[1]);
  register A (.Input(mux16_1_o), .Load(loadA), .Output(A_output));
  and and_6 (ALUtoA, in_1[5], in_1[15]);
  not not_3 (not_3_out, PCload);
  and and_7 (PCload, JumpToA, in_1[15]);
  or or_2 (loadA, ALUtoA, not_1_out);
  or or_3 (JLE, JEQ, JLT);
  register D (.Input(alu_1_out), .Load(loadD), .Output(D_output));
  mux16 mux16_2 (.o(mux16_2_o), .sel(in_1[12]), .b(ram_1_out), .a(A_output));
  pc pc_1 (.Input(A_output), .Output({pc_1_output[15], out_3}), .inc(not_3_out), .load(PCload), .reset(reset));
  or or_4 (JumpToA, JLE, JGT);
  alu alu_1 (
    .x(D_output), .y(mux16_2_o), .ng(ng), .out(alu_1_out), .zr(zr),
    .zx_nx_zy_ny_f_no({in_1[6], in_1[7], in_1[8], in_1[9], in_1[10], in_1[11]}));  // open: Input, Output, inc, load, reset
  Clock clock_1 (.out(CLK));
  RAM ram_1 (.Address(A_output[14:0]), .load(writeM), .in(alu_1_out), .out(ram_1_out));

  // Other names for the same wires on the sheet: A_M = in_1[12];
  //   op_code[5:0] = {in_1[6], in_1[7], in_1[8], in_1[9], in_1[10], in_1[11]}

  // Notes on the sheet:
  //   Decoder
endmodule

// Mux16
module mux16 (
  input  sel,
  input  [15:0] a,
  input  [15:0] b,
  output [15:0] o
);

  Multiplexer #(.enable("false")) multiplexer_1 (.in0(a[0]), .in1(b[0]), .out(o[0]), .sel(sel));
  Multiplexer #(.enable("false")) multiplexer_2 (.in0(a[1]), .in1(b[1]), .out(o[1]), .sel(sel));
  Multiplexer #(.enable("false")) multiplexer_3 (.in0(a[2]), .in1(b[2]), .out(o[2]), .sel(sel));
  Multiplexer #(.enable("false")) multiplexer_4 (.in0(a[4]), .in1(b[4]), .out(o[4]), .sel(sel));
  Multiplexer #(.enable("false")) multiplexer_5 (.in0(a[3]), .in1(b[3]), .out(o[3]), .sel(sel));
  Multiplexer #(.enable("false")) multiplexer_6 (.in0(a[5]), .in1(b[5]), .out(o[5]), .sel(sel));
  Multiplexer #(.enable("false")) multiplexer_7 (.in0(a[6]), .in1(b[6]), .out(o[6]), .sel(sel));
  Multiplexer #(.enable("false")) multiplexer_8 (.in0(a[7]), .in1(b[7]), .out(o[7]), .sel(sel));
  Multiplexer #(.enable("false")) multiplexer_9 (.in0(a[8]), .in1(b[8]), .out(o[8]), .sel(sel));
  Multiplexer #(.enable("false")) multiplexer_10 (.in0(a[9]), .in1(b[9]), .out(o[9]), .sel(sel));
  Multiplexer #(.enable("false")) multiplexer_11 (.in0(a[10]), .in1(b[10]), .out(o[10]), .sel(sel));
  Multiplexer #(.enable("false")) multiplexer_12 (.in0(a[12]), .in1(b[12]), .out(o[12]), .sel(sel));
  Multiplexer #(.enable("false")) multiplexer_13 (.in0(a[11]), .in1(b[11]), .out(o[11]), .sel(sel));
  Multiplexer #(.enable("false")) multiplexer_14 (.in0(a[13]), .in1(b[13]), .out(o[13]), .sel(sel));
  Multiplexer #(.enable("false")) multiplexer_15 (.in0(a[14]), .in1(b[14]), .out(o[14]), .sel(sel));
  Multiplexer #(.enable("false")) multiplexer_16 (.in0(a[15]), .in1(b[15]), .out(o[15]), .sel(sel));
endmodule

// ALU
module alu (
  input  [15:0] x,
  input  [15:0] y,
  input  [5:0] zx_nx_zy_ny_f_no,
  input  [15:0] Input,
  input  inc,
  input  load,
  input  reset,
  output ng,
  output [15:0] out,
  output zr,
  output [15:0] Output
);

  wire clock_1_out, or16way_1_out_2;
  wire [15:0] adder_1_out, adder_2_out, and_1_out, multiplexer_1_out, multiplexer_2_out, multiplexer_3_out,
       multiplexer_4_out, multiplexer_5_out, multiplexer_6_out, not_1_out, not_2_out, not_3_out;

  assign not_1_out = ~x;  // NOT_Gate not_1, 16 bits wide
  assign not_2_out = ~y;  // NOT_Gate not_2, 16 bits wide
  Adder #(.width(16)) adder_1 (.a(Output), .b(16'h1), .out(adder_1_out));  // open: cin, cout
  Multiplexer #(.select(2), .width(16), .enable("false")) multiplexer_1 (
    .in0(x), .in1(not_1_out), .in2({16{1'b0}}), .in3({16{1'b1}}), .out(multiplexer_1_out),
    .sel(zx_nx_zy_ny_f_no[5:4]));
  Multiplexer #(.select(2), .width(16), .enable("false")) multiplexer_2 (
    .in0(y), .in1(not_2_out), .in2({16{1'b0}}), .in3({16{1'b1}}), .out(multiplexer_2_out),
    .sel(zx_nx_zy_ny_f_no[3:2]));
  Multiplexer #(.width(16), .enable("false")) multiplexer_3 (
    .in0(Output), .in1(adder_1_out), .out(multiplexer_3_out), .sel(inc));
  assign and_1_out = multiplexer_1_out & multiplexer_2_out;  // AND_Gate and_1, 16 bits wide
  Adder #(.width(16)) adder_2 (.a(multiplexer_1_out), .b(multiplexer_2_out), .out(adder_2_out));  // open: cin, cout
  Multiplexer #(.width(16), .enable("false")) multiplexer_4 (
    .in0(multiplexer_3_out), .in1(Input), .out(multiplexer_4_out), .sel(load));
  Multiplexer #(.width(16), .enable("false")) multiplexer_5 (
    .in0(multiplexer_4_out), .in1({16{1'b0}}), .out(multiplexer_5_out), .sel(reset));
  Multiplexer #(.width(16), .enable("false")) multiplexer_6 (
    .in0(and_1_out), .in1(adder_2_out), .out(multiplexer_6_out), .sel(zx_nx_zy_ny_f_no[1]));
  assign not_3_out = ~multiplexer_6_out;  // NOT_Gate not_3, 16 bits wide
  Register #(.width(16)) register_1 (.D(multiplexer_5_out), .en(1'b1), .Q(Output), .clk(clock_1_out));  // open: clr
  Clock clock_1 (.out(clock_1_out));
  Multiplexer #(.width(16), .enable("false")) multiplexer_7 (
    .in0(multiplexer_6_out), .in1(not_3_out), .out(out), .sel(zx_nx_zy_ny_f_no[0]));
  and and_2 (ng, out[15], 1'b1);
  Or16Way or16way_1 (.in_1(out), .out_2(or16way_1_out_2));
  not not_4 (zr, or16way_1_out_2);

  // Notes on the sheet:
  //   i: ALU (Arithematic Logic Unit)
  //   ii: PC (Program Counter)
endmodule

module Or16Way (
  input  [15:0] in_1,
  output out_2
);

  wire or_1_out, or_2_out;

  or or_1 (or_1_out, in_1[0], in_1[1], in_1[2], in_1[3], in_1[4], in_1[5], in_1[6], in_1[7]);
  or or_2 (or_2_out, in_1[8], in_1[9], in_1[10], in_1[11], in_1[12], in_1[13], in_1[14], in_1[15]);
  or or_3 (out_2, or_1_out, or_2_out);
endmodule

// PC
module pc (
  input  [15:0] Input,
  input  inc,
  input  load,
  input  reset,
  output [15:0] Output
);

  wire clock_1_out;
  wire [15:0] adder_1_out, multiplexer_1_out, multiplexer_2_out, multiplexer_3_out;

  Multiplexer #(.width(16), .enable("false")) multiplexer_1 (
    .in0(Output), .in1(adder_1_out), .out(multiplexer_1_out), .sel(inc));
  Adder #(.width(16)) adder_1 (.a(Output), .b(16'h1), .out(adder_1_out));  // open: cin, cout
  Multiplexer #(.width(16), .enable("false")) multiplexer_2 (
    .in0(multiplexer_1_out), .in1(Input), .out(multiplexer_2_out), .sel(load));
  Multiplexer #(.width(16), .enable("false")) multiplexer_3 (
    .in0(multiplexer_2_out), .in1({16{1'b0}}), .out(multiplexer_3_out), .sel(reset));
  Clock clock_1 (.out(clock_1_out));
  Register #(.width(16)) register_1 (.D(multiplexer_3_out), .en(1'b1), .Q(Output), .clk(clock_1_out));  // open: clr

  // Notes on the sheet:
  //   PC (Program Counter)
endmodule

module Inc16 (
  input  [15:0] in_1,
  output [15:0] out_2
);

  Adder #(.width(16)) adder_1 (.a(in_1), .b(16'h1), .out(out_2));  // open: cin, cout
endmodule

module register (
  input  [15:0] Input,
  input  Load,
  output [15:0] Output
);

  wire clock_1_out;

  Clock clock_1 (.out(clock_1_out));
  Register #(.width(1)) register_1 (.D(Input[7]), .en(Load), .Q(Output[7]), .clk(clock_1_out));  // open: clr
  Register #(.width(1)) register_2 (.D(Input[6]), .en(Load), .Q(Output[6]), .clk(clock_1_out));  // open: clr
  Register #(.width(1)) register_3 (.D(Input[8]), .en(Load), .Q(Output[8]), .clk(clock_1_out));  // open: clr
  Register #(.width(1)) register_4 (.D(Input[9]), .en(Load), .Q(Output[9]), .clk(clock_1_out));  // open: clr
  Register #(.width(1)) register_5 (.D(Input[5]), .en(Load), .Q(Output[5]), .clk(clock_1_out));  // open: clr
  Register #(.width(1)) register_6 (.D(Input[10]), .en(Load), .Q(Output[10]), .clk(clock_1_out));  // open: clr
  Register #(.width(1)) register_7 (.D(Input[4]), .en(Load), .Q(Output[4]), .clk(clock_1_out));  // open: clr
  Register #(.width(1)) register_8 (.D(Input[11]), .en(Load), .Q(Output[11]), .clk(clock_1_out));  // open: clr
  Register #(.width(1)) register_9 (.D(Input[2]), .en(Load), .Q(Output[2]), .clk(clock_1_out));  // open: clr
  Register #(.width(1)) register_10 (.D(Input[3]), .en(Load), .Q(Output[3]), .clk(clock_1_out));  // open: clr
  Register #(.width(1)) register_11 (.D(Input[13]), .en(Load), .Q(Output[13]), .clk(clock_1_out));  // open: clr
  Register #(.width(1)) register_12 (.D(Input[12]), .en(Load), .Q(Output[12]), .clk(clock_1_out));  // open: clr
  Register #(.width(1)) register_13 (.D(Input[1]), .en(Load), .Q(Output[1]), .clk(clock_1_out));  // open: clr
  Register #(.width(1)) register_14 (.D(Input[14]), .en(Load), .Q(Output[14]), .clk(clock_1_out));  // open: clr
  Register #(.width(1)) register_15 (.D(Input[0]), .en(Load), .Q(Output[0]), .clk(clock_1_out));  // open: clr
  Register #(.width(1)) register_16 (.D(Input[15]), .en(Load), .Q(Output[15]), .clk(clock_1_out));  // open: clr

  // Notes on the sheet:
  //   16-bit Register
endmodule

module Or16 (
  input  [15:0] in_1,
  input  [15:0] in_2,
  output [15:0] out_3
);

  or or_1 (out_3[0], in_1[0], in_2[0]);
  or or_2 (out_3[1], in_1[1], in_2[1]);
  or or_3 (out_3[2], in_1[2], in_2[2]);
  or or_4 (out_3[3], in_1[3], in_2[3]);
  or or_5 (out_3[4], in_1[4], in_2[4]);
  or or_6 (out_3[5], in_1[5], in_2[5]);
  or or_7 (out_3[6], in_1[6], in_2[6]);
  or or_8 (out_3[8], in_1[8], in_2[8]);
  or or_9 (out_3[7], in_1[7], in_2[7]);
  or or_10 (out_3[9], in_1[9], in_2[9]);
  or or_11 (out_3[10], in_1[10], in_2[10]);
  or or_12 (out_3[11], in_1[11], in_2[11]);
  or or_13 (out_3[12], in_1[12], in_2[12]);
  or or_14 (out_3[13], in_1[13], in_2[13]);
  or or_15 (out_3[14], in_1[14], in_2[14]);
  or or_16 (out_3[15], in_1[15], in_2[15]);
endmodule

// RAM16K
module ram16k (
  input  [15:0] Input,
  input  Load,
  input  [13:0] Address,
  output [15:0] Output
);

  wire clock_1_out, demultiplexer_1_out0, demultiplexer_1_out1, demultiplexer_1_out2, demultiplexer_1_out3;
  wire [15:0] ram_1_data, ram_2_data, ram_3_data, ram_4_data;

  Demultiplexer #(.select(2)) demultiplexer_1 (
    .out0(demultiplexer_1_out0), .out1(demultiplexer_1_out1), .out2(demultiplexer_1_out2),
    .out3(demultiplexer_1_out3), .in(Load), .sel(Address[13:12]));  // open: en
  RAM_part #(.addrWidth(12), .dataWidth(16), .bus("separate")) ram_1 (
    .addr(Address[11:0]), .din(Input), .data(ram_1_data), .str(demultiplexer_1_out0), .clk(clock_1_out));  // open: sel, ld, clr
  RAM_part #(.addrWidth(12), .dataWidth(16), .bus("separate")) ram_2 (
    .addr(Address[11:0]), .din(Input), .data(ram_2_data), .str(demultiplexer_1_out2), .clk(clock_1_out));  // open: sel, ld, clr
  Clock clock_1 (.out(clock_1_out));
  RAM_part #(.addrWidth(12), .dataWidth(16), .bus("separate")) ram_3 (
    .addr(Address[11:0]), .din(Input), .data(ram_3_data), .str(demultiplexer_1_out1), .clk(clock_1_out));  // open: sel, ld, clr
  RAM_part #(.addrWidth(12), .dataWidth(16), .bus("separate")) ram_4 (
    .addr(Address[11:0]), .din(Input), .data(ram_4_data), .str(demultiplexer_1_out3), .clk(clock_1_out));  // open: sel, ld, clr
  Multiplexer #(.select(2), .width(16)) multiplexer_1 (
    .in0(ram_1_data), .in1(ram_3_data), .in2(ram_2_data), .in3(ram_4_data), .out(Output), .sel(Address[13:12]));  // open: en

  // Notes on the sheet:
  //   RAM16K
endmodule

module RAM (
  input  [14:0] Address,
  input  load,
  input  [15:0] in,
  output [15:0] out
);

  wire dmux4way_1_out_3, dmux4way_1_out_4, dmux4way_1_out_5, or_1_out;
  wire [15:0] keyboard_1_out_1, ram16k_1_output, screen_1_out_4;

  or or_1 (or_1_out, dmux4way_1_out_3, dmux4way_1_out_4);
  DMux4Way dmux4way_1 (
    .in_1(load), .out_3(dmux4way_1_out_3), .out_4(dmux4way_1_out_4), .out_5(dmux4way_1_out_5),
    .in_2(Address[14:13]));  // open: out_6
  keyboard keyboard_1 (.out_1(keyboard_1_out_1));
  ram16k ram16k_1 (.Load(or_1_out), .Output(ram16k_1_output), .Input(in), .Address(Address[13:0]));
  screen screen_1 (.in_1(in), .in_2(dmux4way_1_out_5), .in_3(Address[12:0]), .out_4(screen_1_out_4));
  Mux4Way16 mux4way16_1 (
    .in_1(ram16k_1_output), .in_2(ram16k_1_output), .in_3(screen_1_out_4), .in_4(keyboard_1_out_1),
    .out_6(out), .in_5(Address[14:13]));
endmodule

// Keyboard
module keyboard (
  output [15:0] out_1
);
endmodule

module Mux4Way16 (
  input  [15:0] in_1,
  input  [15:0] in_2,
  input  [15:0] in_3,
  input  [15:0] in_4,
  input  [1:0] in_5,
  output [15:0] out_6
);

  wire [15:0] multiplexer_1_out, multiplexer_2_out;

  Multiplexer #(.width(16), .enable("false")) multiplexer_1 (
    .in0(in_1), .in1(in_2), .out(multiplexer_1_out), .sel(in_5[0]));
  Multiplexer #(.width(16), .enable("false")) multiplexer_2 (
    .in0(in_3), .in1(in_4), .out(multiplexer_2_out), .sel(in_5[0]));
  Multiplexer #(.width(16), .enable("false")) multiplexer_3 (
    .in0(multiplexer_1_out), .in1(multiplexer_2_out), .out(out_6), .sel(in_5[1]));
endmodule

module DMux4Way (
  input  in_1,
  input  [1:0] in_2,
  output out_3,
  output out_4,
  output out_5,
  output out_6
);

  wire demultiplexer_2_out0, demultiplexer_2_out1;

  Demultiplexer #(.enable("false")) demultiplexer_1 (
    .out0(out_3), .out1(out_4), .in(demultiplexer_2_out0), .sel(in_2[0]));
  Demultiplexer #(.enable("false")) demultiplexer_2 (
    .out0(demultiplexer_2_out0), .out1(demultiplexer_2_out1), .in(in_1), .sel(in_2[1]));
  Demultiplexer #(.enable("false")) demultiplexer_3 (
    .out0(out_5), .out1(out_6), .in(demultiplexer_2_out1), .sel(in_2[0]));
endmodule

// Screen
module screen (
  input  [15:0] in_1,
  input  in_2,
  input  [12:0] in_3,
  output [15:0] out_4
);
endmodule

module ROM (
  input  [14:0] in_1,
  output [15:0] out_2
);
endmodule
